# Fritzing sketch Diagram (saved by Fritzing 0.9.3b)

parts:
  Part1 = sensor_biometrico
  Part2 = RFID-RC522-v2
  Part3 = Arduino Micro (Rev3)

nets:
  VCC: Part1.VCC, Part3.5V
  N1: Part1.TX, Part3.D0/RX
  N2: Part1.RX, Part3.D1/TX
  GND: Part1.GND, Part2.GND, Part3.GND
  N3: Part2.SDA, Part3.D10_PWM/A10
  N4: Part2.SCK, Part3.D13_PWM
  N5: Part2.MOSI, Part3.D11_PWM
  N6: Part2.MISO, Part3.D12_PWM/A11
  N7: Part2.RST, Part3.D9_PWM/A9
  3.3V: Part2.3.3V, Part3.3V3

custom parts:
  sensor_biometrico: Adafruit Optical Fingerprint Sensor
  RFID-RC522-v2: A simple China made RFID-RC522 Reader; do check the pin labels, as this is a MFRC522 based clone.
